# Fritzing sketch Type4-esp-12F-v132-BIGSIZE--SMD1206 (saved by Fritzing 0.9.3b)
circuit board: 8cm x 2.5cm
breadboards: 1

parts:
  ESP-12F = ESP8266 WiFi Module [part_number=ESP8266]
  BC547 = PNP-Transistor [package="TO92 [THT]"]
  DIODE = Rectifier Diode [part_number=1N4001 package="300 mil [THT]"]
  TX/RX = male pin header, 2 pins [form="♂ (male)"]
  470Ω = Resistor [tolerance=±5% resistance=470 package=THT]
  4_7kΩ = Resistor [tolerance=±5% resistance=4.7k package=THT]
  Oled = Grove OLED 128x96
  4_7kΩ_2 = Resistor [tolerance=±5% resistance=4.7k package=THT]
  4_7kΩ_3 = Resistor [tolerance=±5% resistance=4.7k package=THT]
  OLED_BTN = female pin header, 2 pins [form="♀ (female)"]
  RESET = SWITCH-MOMENTARY-2 [package=tactile-switch-1101ne]
  FLASH = SWITCH-MOMENTARY-2 [package=tactile-switch-1101ne]
  10kΩ = Resistor [tolerance=±5% resistance=10k package=THT]
  +DHT- = Header 3 [package=molex-1x3_lock]
  -F2+ = Header 2 [package=molex-1x2_lock]
  -F1+ = Header 2 [package=molex-1x2_lock]
  -+DATA = Header 3 [package=molex-1x3_lock]
  SETUP_BTN = female pin header, 2 pins [form="♀ (female)"]
  10kΩ1 = Resistor [tolerance=±5% resistance=10k package=THT]
  LM1117 = Voltage Regulator LM1117 [package=sot223]
  10uf = Tantalum Capacitor [capacitance=10µF voltage=10V package="200 mil [THT, tantalum]"]
  10uf_2 = Tantalum Capacitor [capacitance=10µF voltage=10V package="200 mil [THT, tantalum]"]

nets:
  N1: ESP-12F.RXD, TX/RX.pin1
  VCC: ESP-12F.VCC, Oled.VCC, 4_7kΩ_2.Pin_0, 4_7kΩ_3.Pin_0, 10kΩ.Pin_1, 10kΩ1.Pin_1, LM1117.OUT, 10uf_2.+
  N2: ESP-12F.GPIO_0, FLASH.1
  N3: ESP-12F.GPIO_2, 4_7kΩ_2.Pin_1
  N4: ESP-12F.EN, 10kΩ.Pin_0
  GND: ESP-12F.GND, BC547.C, 4_7kΩ.Pin_0, Oled.GND, OLED_BTN.pin1, RESET.2, FLASH.2, +DHT-.3, -+DATA.1, SETUP_BTN.pin1, LM1117.ADJ, 10uf.-, 10uf_2.-
  N5: ESP-12F.TXD, TX/RX.pin2
  N6: ESP-12F.GPIO_15, 4_7kΩ.Pin_1
  N7: ESP-12F.GPIO_4, Oled.SDA
  N8: ESP-12F.GPIO_5, Oled.SCL
  N9: ESP-12F.GPIO_16, 470Ω.Pin_1
  N10: ESP-12F.GPIO_14, OLED_BTN.pin2, 10kΩ1.Pin_0
  N11: ESP-12F.GPIO_12, SETUP_BTN.pin2
  N12: ESP-12F.GPIO_13, +DHT-.2
  N13: ESP-12F.REST, 4_7kΩ_3.Pin_1, RESET.1
  N14: BC547.E, DIODE.anode, -F2+.1, -F1+.1, -+DATA.3
  N15: BC547.B, 470Ω.Pin_0
  N16: DIODE.cathode, +DHT-.1, -F2+.2, -F1+.2, -+DATA.2, LM1117.IN, 10uf.+

notes:
  Prog
  Reset
  GND OUT  IN
  GND VCC SCL SDA
  knockimov humidor v1.3.2

custom parts:
  ESP8266 WiFi Module: Generic WiFi Module based on the ESP8266 with onboard PCB antenna and UART communications
